// Logisim project cpu.circ as structural Verilog
module ALU_Input_Stage (
  input  Zero,
  input  Negate,
  input  [7:0] Input,
  output [7:0] out_4
);

  wire not_1_out, not_2_out;
  wire [7:0] controlled_buffer_1_out;

  not not_1 (not_1_out, Zero);
  assign controlled_buffer_1_out = not_1_out ? Input : 8'bz;  // Controlled_Buffer controlled_buffer_1
  assign controlled_buffer_1_out = Zero ? {8{1'b0}} : 8'bz;  // Controlled_Buffer controlled_buffer_2
  not not_2 (not_2_out, Negate);
  assign out_4 = not_2_out ? controlled_buffer_1_out : 8'bz;  // Controlled_Buffer controlled_buffer_3
  assign out_4 = Negate ? ~controlled_buffer_1_out : 8'bz;  // Controlled_Inverter controlled_inverter_1
endmodule
